// Logisim project Logisim_Multiplication_project.circ as structural Verilog: 10 circuits, main circuit ControlUnit
// CU
module ControlUnit (
  input  clk,
  input  rst,
  output EOM
);

  wire and_1_out, and_2_out, and_3_out, d_ff_1_q, d_ff_2_q, d_ff_3_q, d_ff_4_q, multiplexer_1_out,
       multiplexer_2_out, multiplexer_3_out, multiplexer_4_out, not_1_out, xor_1_out, xor_2_out, xor_3_out,
       xor_4_out;

  xor xor_1 (xor_1_out, d_ff_1_q, not_1_out);
  D_Flip_Flop d_ff_1 (.D(multiplexer_1_out), .clk(clk), .Q(d_ff_1_q));  // open: Qn, preset, reset
  Multiplexer multiplexer_1 (.in0(xor_1_out), .in1(1'b0), .out(multiplexer_1_out), .sel(rst));
  and and_1 (and_1_out, d_ff_1_q, not_1_out);
  Multiplexer multiplexer_2 (.in0(xor_2_out), .in1(1'b0), .out(multiplexer_2_out), .sel(rst));
  xor xor_2 (xor_2_out, d_ff_2_q, and_1_out);
  D_Flip_Flop d_ff_2 (.D(multiplexer_2_out), .clk(clk), .Q(d_ff_2_q));  // open: Qn, preset, reset
  xor xor_3 (xor_3_out, d_ff_3_q, and_2_out);
  and and_2 (and_2_out, d_ff_2_q, and_1_out);
  D_Flip_Flop d_ff_3 (.D(multiplexer_3_out), .clk(clk), .Q(d_ff_3_q));  // open: Qn, preset, reset
  Multiplexer multiplexer_3 (.in0(xor_3_out), .in1(1'b0), .out(multiplexer_3_out), .sel(rst));
  D_Flip_Flop d_ff_4 (.D(multiplexer_4_out), .clk(clk), .Q(d_ff_4_q));  // open: Qn, preset, reset
  Multiplexer multiplexer_4 (.in0(xor_4_out), .in1(1'b0), .out(multiplexer_4_out), .sel(rst));
  xor xor_4 (xor_4_out, d_ff_4_q, and_3_out);
  and and_3 (and_3_out, d_ff_3_q, and_2_out);
  and and_4 (EOM, d_ff_1_q, d_ff_4_q);
  not not_1 (not_1_out, EOM);
endmodule

module Main (
  input  [7:0] in_1,
  input  [7:0] in_2
);

  wire and_1_out, btn_out, clk_out, controlunit_1_eom, left_out, not_1_out, register_1_q, right_out,
       xor_1_out;
  wire [1:0] threesvnseg_1_z1;
  wire [6:0] bcdsevseg_1_pin29, bcdsevseg_1_pin36;
  wire [7:0] multiplexer_1_out, multiplexer_2_out, twoscomp8_1_z0, twoscomp8_2_z0;
  wire [15:0] addshiftmultiplier_1_p0;
  wire [20:0] bcdsevseg_1_pin7, multiplexer_3_out;

  Clock #(.phaseOffset(100)) clk (.out(clk_out));
  Button btn (.out(btn_out));
  and and_1 (and_1_out, btn_out, controlunit_1_eom);
  ControlUnit controlunit_1 (.clk(clk_out), .rst(btn_out), .EOM(controlunit_1_eom));
  not not_1 (not_1_out, controlunit_1_eom);
  LED EOM (.in(controlunit_1_eom));
  Multiplexer #(.width(8)) multiplexer_1 (.in0(in_1), .in1(twoscomp8_1_z0), .out(multiplexer_1_out), .sel(in_1[7]));
  twosComp8 twoscomp8_1 (
    .a0(in_1[0]), .a1(in_1[1]), .a2(in_1[2]), .a3(in_1[3]), .a4(in_1[4]), .a5(in_1[5]), .a6(in_1[6]),
    .a7(in_1[7]), .z0(twoscomp8_1_z0[0]), .z1(twoscomp8_1_z0[1]), .z2(twoscomp8_1_z0[2]),
    .z3(twoscomp8_1_z0[3]), .z4(twoscomp8_1_z0[4]), .z5(twoscomp8_1_z0[5]), .z6(twoscomp8_1_z0[6]),
    .z7(twoscomp8_1_z0[7]));
  Multiplexer #(.width(8)) multiplexer_2 (.in0(in_2), .in1(twoscomp8_2_z0), .out(multiplexer_2_out), .sel(in_2[7]));
  addShiftMultiplier addshiftmultiplier_1 (
    .clk(clk_out), .rst(and_1_out), .en(not_1_out), .b0(multiplexer_2_out[0]), .b1(multiplexer_2_out[1]),
    .b2(multiplexer_2_out[2]), .b3(multiplexer_2_out[3]), .b4(multiplexer_2_out[4]),
    .b5(multiplexer_2_out[5]), .b6(multiplexer_2_out[6]), .b7(multiplexer_2_out[7]),
    .a0(multiplexer_1_out[0]), .debouncerBC(btn_out), .a1(multiplexer_1_out[1]), .a2(multiplexer_1_out[2]),
    .a3(multiplexer_1_out[3]), .a4(multiplexer_1_out[4]), .a5(multiplexer_1_out[5]),
    .a6(multiplexer_1_out[6]), .a7(multiplexer_1_out[7]), .p15(addshiftmultiplier_1_p0[15]),
    .out_22(addshiftmultiplier_1_p0[14]), .out_23(addshiftmultiplier_1_p0[13]),
    .out_24(addshiftmultiplier_1_p0[12]), .out_25(addshiftmultiplier_1_p0[11]),
    .out_26(addshiftmultiplier_1_p0[10]), .out_27(addshiftmultiplier_1_p0[9]),
    .out_28(addshiftmultiplier_1_p0[8]), .out_29(addshiftmultiplier_1_p0[7]),
    .out_30(addshiftmultiplier_1_p0[6]), .out_31(addshiftmultiplier_1_p0[5]),
    .out_32(addshiftmultiplier_1_p0[4]), .out_33(addshiftmultiplier_1_p0[3]),
    .out_34(addshiftmultiplier_1_p0[2]), .out_35(addshiftmultiplier_1_p0[1]), .p0(addshiftmultiplier_1_p0[0]));
  twosComp8 twoscomp8_2 (
    .a0(in_2[0]), .a1(in_2[1]), .a2(in_2[2]), .a3(in_2[3]), .a4(in_2[4]), .a5(in_2[5]), .a6(in_2[6]),
    .a7(in_2[7]), .z0(twoscomp8_2_z0[0]), .z1(twoscomp8_2_z0[1]), .z2(twoscomp8_2_z0[2]),
    .z3(twoscomp8_2_z0[3]), .z4(twoscomp8_2_z0[4]), .z5(twoscomp8_2_z0[5]), .z6(twoscomp8_2_z0[6]),
    .z7(twoscomp8_2_z0[7]));
  xor xor_1 (xor_1_out, in_1[7], in_2[7]);
  Register #(.width(1)) register_1 (.D(xor_1_out), .en(and_1_out), .clk(clk_out), .Q(register_1_q));  // open: clr
  bcdsevseg bcdsevseg_1 (
    .msb(addshiftmultiplier_1_p0[15]), .in_2(addshiftmultiplier_1_p0[14]),
    .in_3(addshiftmultiplier_1_p0[13]), .in_4(addshiftmultiplier_1_p0[12]),
    .in_5(addshiftmultiplier_1_p0[11]), .in_6(addshiftmultiplier_1_p0[10]),
    .in_7(addshiftmultiplier_1_p0[9]), .in_8(addshiftmultiplier_1_p0[8]), .in_9(addshiftmultiplier_1_p0[7]),
    .in_10(addshiftmultiplier_1_p0[6]), .in_11(addshiftmultiplier_1_p0[5]),
    .in_12(addshiftmultiplier_1_p0[4]), .in_13(addshiftmultiplier_1_p0[3]),
    .in_14(addshiftmultiplier_1_p0[2]), .in_15(addshiftmultiplier_1_p0[1]), .lsb(addshiftmultiplier_1_p0[0]),
    .pin1(bcdsevseg_1_pin7[20]), .pin2(bcdsevseg_1_pin7[19]), .pin3(bcdsevseg_1_pin7[18]),
    .pin4(bcdsevseg_1_pin7[17]), .pin5(bcdsevseg_1_pin7[16]), .pin6(bcdsevseg_1_pin7[15]),
    .pin7(bcdsevseg_1_pin7[14]), .pin8(bcdsevseg_1_pin7[13]), .pin9(bcdsevseg_1_pin7[12]),
    .pin10(bcdsevseg_1_pin7[11]), .pin11(bcdsevseg_1_pin7[10]), .pin12(bcdsevseg_1_pin7[9]),
    .pin14(bcdsevseg_1_pin7[8]), .pin15(bcdsevseg_1_pin7[7]), .pin16(bcdsevseg_1_pin7[6]),
    .pin17(bcdsevseg_1_pin7[5]), .pin18(bcdsevseg_1_pin7[4]), .pin19(bcdsevseg_1_pin7[3]),
    .pin20(bcdsevseg_1_pin7[2]), .pin21(bcdsevseg_1_pin7[1]), .pin22(bcdsevseg_1_pin7[0]),
    .pin23(bcdsevseg_1_pin29[6]), .pin24(bcdsevseg_1_pin29[5]), .pin25(bcdsevseg_1_pin29[4]),
    .pin26(bcdsevseg_1_pin29[3]), .pin27(bcdsevseg_1_pin29[2]), .pin28(bcdsevseg_1_pin29[1]),
    .pin29(bcdsevseg_1_pin29[0]), .pin30(bcdsevseg_1_pin36[6]), .pin31(bcdsevseg_1_pin36[5]),
    .pin32(bcdsevseg_1_pin36[4]), .pin33(bcdsevseg_1_pin36[3]), .pin34(bcdsevseg_1_pin36[2]),
    .pin35(bcdsevseg_1_pin36[1]), .pin36(bcdsevseg_1_pin36[0]));
  Button left (.out(left_out));
  Button right (.out(right_out));
  threeSvnSeg threesvnseg_1 (.L(left_out), .R(right_out), .Z2(threesvnseg_1_z1[1]), .Z1(threesvnseg_1_z1[0]));
  Multiplexer #(.select(2), .width(21)) multiplexer_3 (
    .in0(bcdsevseg_1_pin7), .in1({bcdsevseg_1_pin7[13:0], bcdsevseg_1_pin29}),
    .in2({bcdsevseg_1_pin7[6:0], bcdsevseg_1_pin29, bcdsevseg_1_pin36}), .out(multiplexer_3_out),
    .sel(threesvnseg_1_z1));  // open: in3
  _7_Segment_Display u_7_segment_display_1 (.g(register_1_q));  // open: f, a, b, e, d, c, dp
  _7_Segment_Display u_7_segment_display_2 (
    .g(multiplexer_3_out[3]), .f(multiplexer_3_out[4]), .a(multiplexer_3_out[5]), .b(multiplexer_3_out[6]),
    .e(multiplexer_3_out[2]), .d(multiplexer_3_out[1]), .c(multiplexer_3_out[0]));  // open: dp
  _7_Segment_Display u_7_segment_display_3 (
    .g(multiplexer_3_out[10]), .f(multiplexer_3_out[11]), .a(multiplexer_3_out[12]),
    .b(multiplexer_3_out[13]), .e(multiplexer_3_out[9]), .d(multiplexer_3_out[8]), .c(multiplexer_3_out[7]));  // open: dp
  _7_Segment_Display u_7_segment_display_4 (
    .g(multiplexer_3_out[17]), .f(multiplexer_3_out[18]), .a(multiplexer_3_out[19]),
    .b(multiplexer_3_out[20]), .e(multiplexer_3_out[16]), .d(multiplexer_3_out[15]), .c(multiplexer_3_out[14]));  // open: dp
endmodule

module bcdsevseg (
  input  msb,
  input  in_2,
  input  in_3,
  input  in_4,
  input  in_5,
  input  in_6,
  input  in_7,
  input  in_8,
  input  in_9,
  input  in_10,
  input  in_11,
  input  in_12,
  input  in_13,
  input  in_14,
  input  in_15,
  input  lsb,
  output pin1,
  output pin2,
  output pin3,
  output pin4,
  output pin5,
  output pin6,
  output pin7,
  output pin8,
  output pin9,
  output pin10,
  output pin11,
  output pin12,
  output pin14,
  output pin15,
  output pin16,
  output pin17,
  output pin18,
  output pin19,
  output pin20,
  output pin21,
  output pin22,
  output pin23,
  output pin24,
  output pin25,
  output pin26,
  output pin27,
  output pin28,
  output pin29,
  output pin30,
  output pin31,
  output pin32,
  output pin33,
  output pin34,
  output pin35,
  output pin36
);

  wire adding_chip_cc7e0fc6_1_s0, adding_chip_cc7e0fc6_1_s1, adding_chip_cc7e0fc6_1_s2,
       adding_chip_cc7e0fc6_1_s3, adding_chip_cc7e0fc6_2_s0, adding_chip_cc7e0fc6_2_s1,
       adding_chip_cc7e0fc6_2_s2, adding_chip_cc7e0fc6_2_s3, adding_chip_cc7e0fc6_3_s0,
       adding_chip_cc7e0fc6_3_s1, adding_chip_cc7e0fc6_3_s2, adding_chip_cc7e0fc6_3_s3,
       adding_chip_cc7e0fc6_4_s0, adding_chip_cc7e0fc6_4_s1, adding_chip_cc7e0fc6_4_s2,
       adding_chip_cc7e0fc6_4_s3, adding_chip_cc7e0fc6_5_s0, adding_chip_cc7e0fc6_5_s1,
       adding_chip_cc7e0fc6_5_s2, adding_chip_cc7e0fc6_5_s3, adding_chip_cc7e0fc6_6_s0,
       adding_chip_cc7e0fc6_6_s1, adding_chip_cc7e0fc6_6_s2, adding_chip_cc7e0fc6_6_s3,
       adding_chip_cc7e0fc6_7_s0, adding_chip_cc7e0fc6_7_s1, adding_chip_cc7e0fc6_7_s2,
       adding_chip_cc7e0fc6_7_s3, adding_chip_cc7e0fc6_8_s0, adding_chip_cc7e0fc6_8_s1,
       adding_chip_cc7e0fc6_8_s2, adding_chip_cc7e0fc6_8_s3, adding_chip_cc7e0fc6_9_s0,
       adding_chip_cc7e0fc6_9_s1, adding_chip_cc7e0fc6_9_s2, adding_chip_cc7e0fc6_9_s3,
       adding_chip_cc7e0fc6_10_s0, adding_chip_cc7e0fc6_10_s1, adding_chip_cc7e0fc6_10_s2,
       adding_chip_cc7e0fc6_10_s3, adding_chip_cc7e0fc6_11_s0, adding_chip_cc7e0fc6_11_s1,
       adding_chip_cc7e0fc6_11_s2, adding_chip_cc7e0fc6_11_s3, adding_chip_cc7e0fc6_12_s0,
       adding_chip_cc7e0fc6_12_s1, adding_chip_cc7e0fc6_12_s2, adding_chip_cc7e0fc6_12_s3,
       adding_chip_cc7e0fc6_13_s0, adding_chip_cc7e0fc6_13_s1, adding_chip_cc7e0fc6_13_s2,
       adding_chip_cc7e0fc6_13_s3, adding_chip_cc7e0fc6_14_s0, adding_chip_cc7e0fc6_14_s1,
       adding_chip_cc7e0fc6_14_s2, adding_chip_cc7e0fc6_14_s3, adding_chip_cc7e0fc6_15_s0,
       adding_chip_cc7e0fc6_15_s1, adding_chip_cc7e0fc6_15_s2, adding_chip_cc7e0fc6_15_s3,
       adding_chip_cc7e0fc6_16_s0, adding_chip_cc7e0fc6_16_s1, adding_chip_cc7e0fc6_16_s2,
       adding_chip_cc7e0fc6_16_s3, adding_chip_cc7e0fc6_17_s0, adding_chip_cc7e0fc6_17_s1,
       adding_chip_cc7e0fc6_17_s2, adding_chip_cc7e0fc6_17_s3, adding_chip_cc7e0fc6_18_s0,
       adding_chip_cc7e0fc6_18_s1, adding_chip_cc7e0fc6_18_s2, adding_chip_cc7e0fc6_18_s3,
       adding_chip_cc7e0fc6_19_s0, adding_chip_cc7e0fc6_19_s1, adding_chip_cc7e0fc6_19_s2,
       adding_chip_cc7e0fc6_19_s3, adding_chip_cc7e0fc6_20_s0, adding_chip_cc7e0fc6_20_s1,
       adding_chip_cc7e0fc6_20_s2, adding_chip_cc7e0fc6_20_s3, adding_chip_cc7e0fc6_21_s0,
       adding_chip_cc7e0fc6_21_s1, adding_chip_cc7e0fc6_21_s2, adding_chip_cc7e0fc6_21_s3,
       adding_chip_cc7e0fc6_22_s0, adding_chip_cc7e0fc6_22_s1, adding_chip_cc7e0fc6_22_s2,
       adding_chip_cc7e0fc6_22_s3, adding_chip_cc7e0fc6_23_s0, adding_chip_cc7e0fc6_23_s1,
       adding_chip_cc7e0fc6_23_s2, adding_chip_cc7e0fc6_23_s3, adding_chip_cc7e0fc6_24_s0,
       adding_chip_cc7e0fc6_24_s1, adding_chip_cc7e0fc6_24_s2, adding_chip_cc7e0fc6_24_s3,
       adding_chip_cc7e0fc6_25_s0, adding_chip_cc7e0fc6_25_s1, adding_chip_cc7e0fc6_25_s2,
       adding_chip_cc7e0fc6_25_s3, adding_chip_cc7e0fc6_26_s0, adding_chip_cc7e0fc6_26_s1,
       adding_chip_cc7e0fc6_26_s2, adding_chip_cc7e0fc6_26_s3, adding_chip_cc7e0fc6_27_s0,
       adding_chip_cc7e0fc6_27_s1, adding_chip_cc7e0fc6_27_s2, adding_chip_cc7e0fc6_27_s3,
       adding_chip_cc7e0fc6_28_s0, adding_chip_cc7e0fc6_28_s1, adding_chip_cc7e0fc6_28_s2,
       adding_chip_cc7e0fc6_28_s3, adding_chip_cc7e0fc6_29_s0, adding_chip_cc7e0fc6_29_s1,
       adding_chip_cc7e0fc6_29_s2, adding_chip_cc7e0fc6_29_s3, adding_chip_cc7e0fc6_30_s0,
       adding_chip_cc7e0fc6_30_s1, adding_chip_cc7e0fc6_30_s2, adding_chip_cc7e0fc6_30_s3,
       adding_chip_cc7e0fc6_31_s0, adding_chip_cc7e0fc6_31_s1, adding_chip_cc7e0fc6_31_s2,
       adding_chip_cc7e0fc6_31_s3, adding_chip_cc7e0fc6_32_s0, adding_chip_cc7e0fc6_32_s1,
       adding_chip_cc7e0fc6_32_s2, adding_chip_cc7e0fc6_32_s3, adding_chip_cc7e0fc6_33_s0,
       adding_chip_cc7e0fc6_33_s1, adding_chip_cc7e0fc6_33_s2, adding_chip_cc7e0fc6_33_s3,
       adding_chip_cc7e0fc6_34_s0, adding_chip_cc7e0fc6_34_s1, adding_chip_cc7e0fc6_34_s2,
       adding_chip_cc7e0fc6_34_s3;

  BCD_to_7_segment_709ac293 bcd_to_7_segment_709ac293_1 (
    .in_1(adding_chip_cc7e0fc6_27_s3), .C(adding_chip_cc7e0fc6_6_s3), .in_3(adding_chip_cc7e0fc6_5_s3),
    .A(adding_chip_cc7e0fc6_4_s3), .B(pin30), .out_6(pin31), .out_7(pin32), .out_8(pin33), .out_9(pin34),
    .D(pin35), .out_11(pin36));
  Adding_chip_cc7e0fc6 adding_chip_cc7e0fc6_1 (
    .A0(adding_chip_cc7e0fc6_9_s3), .A1(adding_chip_cc7e0fc6_8_s3), .A2(adding_chip_cc7e0fc6_7_s3),
    .A3(1'b0), .S0(adding_chip_cc7e0fc6_1_s0), .S1(adding_chip_cc7e0fc6_1_s1),
    .S2(adding_chip_cc7e0fc6_1_s2), .S3(adding_chip_cc7e0fc6_1_s3));
  Adding_chip_cc7e0fc6 adding_chip_cc7e0fc6_2 (
    .A0(adding_chip_cc7e0fc6_13_s3), .A1(adding_chip_cc7e0fc6_11_s3), .A2(adding_chip_cc7e0fc6_1_s3),
    .A3(1'b0), .S0(adding_chip_cc7e0fc6_2_s0), .S1(adding_chip_cc7e0fc6_2_s1),
    .S2(adding_chip_cc7e0fc6_2_s2), .S3(adding_chip_cc7e0fc6_2_s3));
  Adding_chip_cc7e0fc6 adding_chip_cc7e0fc6_3 (
    .A0(adding_chip_cc7e0fc6_15_s3), .A1(adding_chip_cc7e0fc6_2_s0), .A2(adding_chip_cc7e0fc6_2_s1),
    .A3(adding_chip_cc7e0fc6_2_s2), .S0(adding_chip_cc7e0fc6_3_s0), .S1(adding_chip_cc7e0fc6_3_s1),
    .S2(adding_chip_cc7e0fc6_3_s2), .S3(adding_chip_cc7e0fc6_3_s3));
  Adding_chip_cc7e0fc6 adding_chip_cc7e0fc6_4 (
    .A0(adding_chip_cc7e0fc6_19_s3), .A1(adding_chip_cc7e0fc6_3_s3), .A2(adding_chip_cc7e0fc6_2_s3),
    .A3(1'b0), .S0(adding_chip_cc7e0fc6_4_s0), .S1(adding_chip_cc7e0fc6_4_s1),
    .S2(adding_chip_cc7e0fc6_4_s2), .S3(adding_chip_cc7e0fc6_4_s3));
  Adding_chip_cc7e0fc6 adding_chip_cc7e0fc6_5 (
    .A0(adding_chip_cc7e0fc6_21_s3), .A1(adding_chip_cc7e0fc6_4_s0), .A2(adding_chip_cc7e0fc6_4_s1),
    .A3(adding_chip_cc7e0fc6_4_s2), .S0(adding_chip_cc7e0fc6_5_s0), .S1(adding_chip_cc7e0fc6_5_s1),
    .S2(adding_chip_cc7e0fc6_5_s2), .S3(adding_chip_cc7e0fc6_5_s3));
  Adding_chip_cc7e0fc6 adding_chip_cc7e0fc6_6 (
    .A0(adding_chip_cc7e0fc6_23_s3), .A1(adding_chip_cc7e0fc6_5_s0), .A2(adding_chip_cc7e0fc6_5_s1),
    .A3(adding_chip_cc7e0fc6_5_s2), .S0(adding_chip_cc7e0fc6_6_s0), .S1(adding_chip_cc7e0fc6_6_s1),
    .S2(adding_chip_cc7e0fc6_6_s2), .S3(adding_chip_cc7e0fc6_6_s3));
  BCD_to_7_segment_709ac293 bcd_to_7_segment_709ac293_2 (
    .in_1(adding_chip_cc7e0fc6_28_s3), .C(adding_chip_cc7e0fc6_27_s0), .in_3(adding_chip_cc7e0fc6_27_s1),
    .A(adding_chip_cc7e0fc6_27_s2), .B(pin23), .out_6(pin24), .out_7(pin25), .out_8(pin26), .out_9(pin27),
    .D(pin28), .out_11(pin29));
  Adding_chip_cc7e0fc6 adding_chip_cc7e0fc6_7 (
    .A0(in_3), .A1(in_2), .A2(msb), .A3(1'b0), .S0(adding_chip_cc7e0fc6_7_s0),
    .S1(adding_chip_cc7e0fc6_7_s1), .S2(adding_chip_cc7e0fc6_7_s2), .S3(adding_chip_cc7e0fc6_7_s3));
  Adding_chip_cc7e0fc6 adding_chip_cc7e0fc6_8 (
    .A0(in_4), .A1(adding_chip_cc7e0fc6_7_s0), .A2(adding_chip_cc7e0fc6_7_s1),
    .A3(adding_chip_cc7e0fc6_7_s2), .S0(adding_chip_cc7e0fc6_8_s0), .S1(adding_chip_cc7e0fc6_8_s1),
    .S2(adding_chip_cc7e0fc6_8_s2), .S3(adding_chip_cc7e0fc6_8_s3));
  Adding_chip_cc7e0fc6 adding_chip_cc7e0fc6_9 (
    .A0(in_5), .A1(adding_chip_cc7e0fc6_8_s0), .A2(adding_chip_cc7e0fc6_8_s1),
    .A3(adding_chip_cc7e0fc6_8_s2), .S0(adding_chip_cc7e0fc6_9_s0), .S1(adding_chip_cc7e0fc6_9_s1),
    .S2(adding_chip_cc7e0fc6_9_s2), .S3(adding_chip_cc7e0fc6_9_s3));
  Adding_chip_cc7e0fc6 adding_chip_cc7e0fc6_10 (
    .A0(in_6), .A1(adding_chip_cc7e0fc6_9_s0), .A2(adding_chip_cc7e0fc6_9_s1),
    .A3(adding_chip_cc7e0fc6_9_s2), .S0(adding_chip_cc7e0fc6_10_s0), .S1(adding_chip_cc7e0fc6_10_s1),
    .S2(adding_chip_cc7e0fc6_10_s2), .S3(adding_chip_cc7e0fc6_10_s3));
  Adding_chip_cc7e0fc6 adding_chip_cc7e0fc6_11 (
    .A0(adding_chip_cc7e0fc6_10_s3), .A1(adding_chip_cc7e0fc6_1_s0), .A2(adding_chip_cc7e0fc6_1_s1),
    .A3(adding_chip_cc7e0fc6_1_s2), .S0(adding_chip_cc7e0fc6_11_s0), .S1(adding_chip_cc7e0fc6_11_s1),
    .S2(adding_chip_cc7e0fc6_11_s2), .S3(adding_chip_cc7e0fc6_11_s3));
  Adding_chip_cc7e0fc6 adding_chip_cc7e0fc6_12 (
    .A0(in_7), .A1(adding_chip_cc7e0fc6_10_s0), .A2(adding_chip_cc7e0fc6_10_s1),
    .A3(adding_chip_cc7e0fc6_10_s2), .S0(adding_chip_cc7e0fc6_12_s0), .S1(adding_chip_cc7e0fc6_12_s1),
    .S2(adding_chip_cc7e0fc6_12_s2), .S3(adding_chip_cc7e0fc6_12_s3));
  Adding_chip_cc7e0fc6 adding_chip_cc7e0fc6_13 (
    .A0(adding_chip_cc7e0fc6_12_s3), .A1(adding_chip_cc7e0fc6_11_s0), .A2(adding_chip_cc7e0fc6_11_s1),
    .A3(adding_chip_cc7e0fc6_11_s2), .S0(adding_chip_cc7e0fc6_13_s0), .S1(adding_chip_cc7e0fc6_13_s1),
    .S2(adding_chip_cc7e0fc6_13_s2), .S3(adding_chip_cc7e0fc6_13_s3));
  Adding_chip_cc7e0fc6 adding_chip_cc7e0fc6_14 (
    .A0(in_8), .A1(adding_chip_cc7e0fc6_12_s0), .A2(adding_chip_cc7e0fc6_12_s1),
    .A3(adding_chip_cc7e0fc6_12_s2), .S0(adding_chip_cc7e0fc6_14_s0), .S1(adding_chip_cc7e0fc6_14_s1),
    .S2(adding_chip_cc7e0fc6_14_s2), .S3(adding_chip_cc7e0fc6_14_s3));
  Adding_chip_cc7e0fc6 adding_chip_cc7e0fc6_15 (
    .A0(adding_chip_cc7e0fc6_14_s3), .A1(adding_chip_cc7e0fc6_13_s0), .A2(adding_chip_cc7e0fc6_13_s1),
    .A3(adding_chip_cc7e0fc6_13_s2), .S0(adding_chip_cc7e0fc6_15_s0), .S1(adding_chip_cc7e0fc6_15_s1),
    .S2(adding_chip_cc7e0fc6_15_s2), .S3(adding_chip_cc7e0fc6_15_s3));
  Adding_chip_cc7e0fc6 adding_chip_cc7e0fc6_16 (
    .A0(in_9), .A1(adding_chip_cc7e0fc6_14_s0), .A2(adding_chip_cc7e0fc6_14_s1),
    .A3(adding_chip_cc7e0fc6_14_s2), .S0(adding_chip_cc7e0fc6_16_s0), .S1(adding_chip_cc7e0fc6_16_s1),
    .S2(adding_chip_cc7e0fc6_16_s2), .S3(adding_chip_cc7e0fc6_16_s3));
  Adding_chip_cc7e0fc6 adding_chip_cc7e0fc6_17 (
    .A0(adding_chip_cc7e0fc6_16_s3), .A1(adding_chip_cc7e0fc6_15_s0), .A2(adding_chip_cc7e0fc6_15_s1),
    .A3(adding_chip_cc7e0fc6_15_s2), .S0(adding_chip_cc7e0fc6_17_s0), .S1(adding_chip_cc7e0fc6_17_s1),
    .S2(adding_chip_cc7e0fc6_17_s2), .S3(adding_chip_cc7e0fc6_17_s3));
  Adding_chip_cc7e0fc6 adding_chip_cc7e0fc6_18 (
    .A0(in_10), .A1(adding_chip_cc7e0fc6_16_s0), .A2(adding_chip_cc7e0fc6_16_s1),
    .A3(adding_chip_cc7e0fc6_16_s2), .S0(adding_chip_cc7e0fc6_18_s0), .S1(adding_chip_cc7e0fc6_18_s1),
    .S2(adding_chip_cc7e0fc6_18_s2), .S3(adding_chip_cc7e0fc6_18_s3));
  Adding_chip_cc7e0fc6 adding_chip_cc7e0fc6_19 (
    .A0(adding_chip_cc7e0fc6_17_s3), .A1(adding_chip_cc7e0fc6_3_s0), .A2(adding_chip_cc7e0fc6_3_s1),
    .A3(adding_chip_cc7e0fc6_3_s2), .S0(adding_chip_cc7e0fc6_19_s0), .S1(adding_chip_cc7e0fc6_19_s1),
    .S2(adding_chip_cc7e0fc6_19_s2), .S3(adding_chip_cc7e0fc6_19_s3));
  Adding_chip_cc7e0fc6 adding_chip_cc7e0fc6_20 (
    .A0(adding_chip_cc7e0fc6_18_s3), .A1(adding_chip_cc7e0fc6_17_s0), .A2(adding_chip_cc7e0fc6_17_s1),
    .A3(adding_chip_cc7e0fc6_17_s2), .S0(adding_chip_cc7e0fc6_20_s0), .S1(adding_chip_cc7e0fc6_20_s1),
    .S2(adding_chip_cc7e0fc6_20_s2), .S3(adding_chip_cc7e0fc6_20_s3));
  Adding_chip_cc7e0fc6 adding_chip_cc7e0fc6_21 (
    .A0(adding_chip_cc7e0fc6_20_s3), .A1(adding_chip_cc7e0fc6_19_s0), .A2(adding_chip_cc7e0fc6_19_s1),
    .A3(adding_chip_cc7e0fc6_19_s2), .S0(adding_chip_cc7e0fc6_21_s0), .S1(adding_chip_cc7e0fc6_21_s1),
    .S2(adding_chip_cc7e0fc6_21_s2), .S3(adding_chip_cc7e0fc6_21_s3));
  Adding_chip_cc7e0fc6 adding_chip_cc7e0fc6_22 (
    .A0(adding_chip_cc7e0fc6_29_s3), .A1(adding_chip_cc7e0fc6_20_s0), .A2(adding_chip_cc7e0fc6_20_s1),
    .A3(adding_chip_cc7e0fc6_20_s2), .S0(adding_chip_cc7e0fc6_22_s0), .S1(adding_chip_cc7e0fc6_22_s1),
    .S2(adding_chip_cc7e0fc6_22_s2), .S3(adding_chip_cc7e0fc6_22_s3));
  Adding_chip_cc7e0fc6 adding_chip_cc7e0fc6_23 (
    .A0(adding_chip_cc7e0fc6_22_s3), .A1(adding_chip_cc7e0fc6_21_s0), .A2(adding_chip_cc7e0fc6_21_s1),
    .A3(adding_chip_cc7e0fc6_21_s2), .S0(adding_chip_cc7e0fc6_23_s0), .S1(adding_chip_cc7e0fc6_23_s1),
    .S2(adding_chip_cc7e0fc6_23_s2), .S3(adding_chip_cc7e0fc6_23_s3));
  Adding_chip_cc7e0fc6 adding_chip_cc7e0fc6_24 (
    .A0(adding_chip_cc7e0fc6_30_s3), .A1(adding_chip_cc7e0fc6_22_s0), .A2(adding_chip_cc7e0fc6_22_s1),
    .A3(adding_chip_cc7e0fc6_22_s2), .S0(adding_chip_cc7e0fc6_24_s0), .S1(adding_chip_cc7e0fc6_24_s1),
    .S2(adding_chip_cc7e0fc6_24_s2), .S3(adding_chip_cc7e0fc6_24_s3));
  Adding_chip_cc7e0fc6 adding_chip_cc7e0fc6_25 (
    .A0(adding_chip_cc7e0fc6_24_s3), .A1(adding_chip_cc7e0fc6_23_s0), .A2(adding_chip_cc7e0fc6_23_s1),
    .A3(adding_chip_cc7e0fc6_23_s2), .S0(adding_chip_cc7e0fc6_25_s0), .S1(adding_chip_cc7e0fc6_25_s1),
    .S2(adding_chip_cc7e0fc6_25_s2), .S3(adding_chip_cc7e0fc6_25_s3));
  Adding_chip_cc7e0fc6 adding_chip_cc7e0fc6_26 (
    .A0(adding_chip_cc7e0fc6_31_s3), .A1(adding_chip_cc7e0fc6_24_s0), .A2(adding_chip_cc7e0fc6_24_s1),
    .A3(adding_chip_cc7e0fc6_24_s2), .S0(adding_chip_cc7e0fc6_26_s0), .S1(adding_chip_cc7e0fc6_26_s1),
    .S2(adding_chip_cc7e0fc6_26_s2), .S3(adding_chip_cc7e0fc6_26_s3));
  Adding_chip_cc7e0fc6 adding_chip_cc7e0fc6_27 (
    .A0(adding_chip_cc7e0fc6_25_s3), .A1(adding_chip_cc7e0fc6_6_s0), .A2(adding_chip_cc7e0fc6_6_s1),
    .A3(adding_chip_cc7e0fc6_6_s2), .S0(adding_chip_cc7e0fc6_27_s0), .S1(adding_chip_cc7e0fc6_27_s1),
    .S2(adding_chip_cc7e0fc6_27_s2), .S3(adding_chip_cc7e0fc6_27_s3));
  Adding_chip_cc7e0fc6 adding_chip_cc7e0fc6_28 (
    .A0(adding_chip_cc7e0fc6_26_s3), .A1(adding_chip_cc7e0fc6_25_s0), .A2(adding_chip_cc7e0fc6_25_s1),
    .A3(adding_chip_cc7e0fc6_25_s2), .S0(adding_chip_cc7e0fc6_28_s0), .S1(adding_chip_cc7e0fc6_28_s1),
    .S2(adding_chip_cc7e0fc6_28_s2), .S3(adding_chip_cc7e0fc6_28_s3));
  BCD_to_7_segment_709ac293 bcd_to_7_segment_709ac293_3 (
    .in_1(adding_chip_cc7e0fc6_33_s3), .C(adding_chip_cc7e0fc6_28_s0), .in_3(adding_chip_cc7e0fc6_28_s1),
    .A(adding_chip_cc7e0fc6_28_s2), .B(pin16), .out_6(pin17), .out_7(pin18), .out_8(pin19), .out_9(pin20),
    .D(pin21), .out_11(pin22));
  Adding_chip_cc7e0fc6 adding_chip_cc7e0fc6_29 (
    .A0(in_11), .A1(adding_chip_cc7e0fc6_18_s0), .A2(adding_chip_cc7e0fc6_18_s1),
    .A3(adding_chip_cc7e0fc6_18_s2), .S0(adding_chip_cc7e0fc6_29_s0), .S1(adding_chip_cc7e0fc6_29_s1),
    .S2(adding_chip_cc7e0fc6_29_s2), .S3(adding_chip_cc7e0fc6_29_s3));
  Adding_chip_cc7e0fc6 adding_chip_cc7e0fc6_30 (
    .A0(in_12), .A1(adding_chip_cc7e0fc6_29_s0), .A2(adding_chip_cc7e0fc6_29_s1),
    .A3(adding_chip_cc7e0fc6_29_s2), .S0(adding_chip_cc7e0fc6_30_s0), .S1(adding_chip_cc7e0fc6_30_s1),
    .S2(adding_chip_cc7e0fc6_30_s2), .S3(adding_chip_cc7e0fc6_30_s3));
  Adding_chip_cc7e0fc6 adding_chip_cc7e0fc6_31 (
    .A0(in_13), .A1(adding_chip_cc7e0fc6_30_s0), .A2(adding_chip_cc7e0fc6_30_s1),
    .A3(adding_chip_cc7e0fc6_30_s2), .S0(adding_chip_cc7e0fc6_31_s0), .S1(adding_chip_cc7e0fc6_31_s1),
    .S2(adding_chip_cc7e0fc6_31_s2), .S3(adding_chip_cc7e0fc6_31_s3));
  Adding_chip_cc7e0fc6 adding_chip_cc7e0fc6_32 (
    .A0(in_14), .A1(adding_chip_cc7e0fc6_31_s0), .A2(adding_chip_cc7e0fc6_31_s1),
    .A3(adding_chip_cc7e0fc6_31_s2), .S0(adding_chip_cc7e0fc6_32_s0), .S1(adding_chip_cc7e0fc6_32_s1),
    .S2(adding_chip_cc7e0fc6_32_s2), .S3(adding_chip_cc7e0fc6_32_s3));
  Adding_chip_cc7e0fc6 adding_chip_cc7e0fc6_33 (
    .A0(adding_chip_cc7e0fc6_32_s3), .A1(adding_chip_cc7e0fc6_26_s0), .A2(adding_chip_cc7e0fc6_26_s1),
    .A3(adding_chip_cc7e0fc6_26_s2), .S0(adding_chip_cc7e0fc6_33_s0), .S1(adding_chip_cc7e0fc6_33_s1),
    .S2(adding_chip_cc7e0fc6_33_s2), .S3(adding_chip_cc7e0fc6_33_s3));
  Adding_chip_cc7e0fc6 adding_chip_cc7e0fc6_34 (
    .A0(in_15), .A1(adding_chip_cc7e0fc6_32_s0), .A2(adding_chip_cc7e0fc6_32_s1),
    .A3(adding_chip_cc7e0fc6_32_s2), .S0(adding_chip_cc7e0fc6_34_s0), .S1(adding_chip_cc7e0fc6_34_s1),
    .S2(adding_chip_cc7e0fc6_34_s2), .S3(adding_chip_cc7e0fc6_34_s3));
  BCD_to_7_segment_709ac293 bcd_to_7_segment_709ac293_4 (
    .in_1(lsb), .C(adding_chip_cc7e0fc6_34_s0), .in_3(adding_chip_cc7e0fc6_34_s1),
    .A(adding_chip_cc7e0fc6_34_s2), .B(pin1), .out_6(pin2), .out_7(pin3), .out_8(pin4), .out_9(pin5),
    .D(pin6), .out_11(pin7));
  BCD_to_7_segment_709ac293 bcd_to_7_segment_709ac293_5 (
    .in_1(adding_chip_cc7e0fc6_34_s3), .C(adding_chip_cc7e0fc6_33_s0), .in_3(adding_chip_cc7e0fc6_33_s1),
    .A(adding_chip_cc7e0fc6_33_s2), .B(pin8), .out_6(pin9), .out_7(pin10), .out_8(pin11), .out_9(pin12),
    .D(pin14), .out_11(pin15));

  // Notes on the sheet:
  //   Bits from 0 to 15 LSB down
endmodule

module Adding_chip_cc7e0fc6 (
  input  A0,
  input  A1,
  input  A2,
  input  A3,
  output S0,
  output S1,
  output S2,
  output S3
);

  wire and_1_out, and_2_out, and_3_out, and_4_out, and_5_out, and_6_out, and_7_out, and_8_out, and_9_out,
       not_1_out, not_2_out, not_3_out, not_4_out;

  not not_1 (not_1_out, A3);
  not not_2 (not_2_out, A2);
  not not_3 (not_3_out, A1);
  not not_4 (not_4_out, A0);
  and and_1 (and_1_out, A2, A0);
  and and_2 (and_2_out, A2, A1);
  and and_3 (and_3_out, A2, not_3_out, not_4_out);
  and and_4 (and_4_out, A3, A0);
  and and_5 (and_5_out, not_2_out, A1);
  and and_6 (and_6_out, A1, A0);
  and and_7 (and_7_out, A3, not_4_out);
  and and_8 (and_8_out, A2, A1, not_4_out);
  and and_9 (and_9_out, not_1_out, not_2_out, A0);
  or or_1 (S3, and_1_out, and_2_out, A3);
  or or_2 (S2, and_3_out, and_4_out);
  or or_3 (S1, and_5_out, and_6_out, and_7_out);
  or or_4 (S0, and_7_out, and_8_out, and_9_out);
endmodule

module BCD_to_7_segment_709ac293 (
  input  in_1,
  input  C,
  input  in_3,
  input  A,
  output B,
  output out_6,
  output out_7,
  output out_8,
  output out_9,
  output D,
  output out_11
);

  wire and_1_out, and_2_out, and_3_out, and_4_out, and_5_out, and_6_out, and_7_out, and_8_out, and_9_out,
       and_10_out, and_11_out, and_12_out, and_13_out, and_14_out, and_15_out, and_16_out, not_1_out,
       not_2_out, not_3_out;

  or or_1 (out_6, and_1_out, and_2_out, A, C);
  and and_1 (and_1_out, in_3, in_1);
  and and_2 (and_2_out, not_3_out, not_1_out);
  not not_1 (not_1_out, in_1);
  not not_2 (not_2_out, C);
  not not_3 (not_3_out, in_3);
  or or_2 (B, and_3_out, and_4_out, not_3_out);
  and and_3 (and_3_out, C, in_1);
  and and_4 (and_4_out, not_2_out, not_1_out);
  or or_3 (D, and_5_out, and_6_out, and_7_out, and_8_out, A);
  or or_4 (out_11, in_3, not_2_out, in_1);
  and and_5 (and_5_out, C, not_1_out);
  and and_6 (and_6_out, not_3_out, C);
  and and_7 (and_7_out, not_3_out, not_1_out);
  and and_8 (and_8_out, in_3, not_2_out, in_1);
  or E (out_9, and_9_out, and_10_out);
  and and_9 (and_9_out, C, not_1_out);
  and and_10 (and_10_out, not_3_out, not_1_out);
  or F (out_7, and_11_out, and_12_out, and_13_out, A);
  and and_11 (and_11_out, not_2_out, not_1_out);
  and and_12 (and_12_out, in_3, not_1_out);
  and and_13 (and_13_out, in_3, not_2_out);
  or G (out_8, and_14_out, and_15_out, and_16_out, A);
  and and_14 (and_14_out, C, not_1_out);
  and and_15 (and_15_out, in_3, not_2_out);
  and and_16 (and_16_out, not_3_out, C);
endmodule

module RCA8Bits (
  input  cin,
  input  a0,
  input  b0,
  input  a1,
  input  b1,
  input  a2,
  input  b2,
  input  a3,
  input  b3,
  input  a4,
  input  b4,
  input  a5,
  input  b5,
  input  a6,
  input  b6,
  input  a7,
  input  b7,
  output s0,
  output s1,
  output s2,
  output s3,
  output s4,
  output s5,
  output s6,
  output s7,
  output c
);

  wire adder_1_cout, adder_2_cout, adder_3_cout, adder_4_cout, adder_5_cout, adder_6_cout, adder_7_cout;

  Adder #(.width(1)) adder_1 (.a(a0), .b(b0), .out(s0), .cin(cin), .cout(adder_1_cout));
  Adder #(.width(1)) adder_2 (.a(a1), .b(b1), .out(s1), .cin(adder_1_cout), .cout(adder_2_cout));
  Adder #(.width(1)) adder_3 (.a(a2), .b(b2), .out(s2), .cin(adder_2_cout), .cout(adder_3_cout));
  Adder #(.width(1)) adder_4 (.a(a3), .b(b3), .out(s3), .cin(adder_3_cout), .cout(adder_4_cout));
  Adder #(.width(1)) adder_5 (.a(a4), .b(b4), .out(s4), .cin(adder_4_cout), .cout(adder_5_cout));
  Adder #(.width(1)) adder_6 (.a(a5), .b(b5), .out(s5), .cin(adder_5_cout), .cout(adder_6_cout));
  Adder #(.width(1)) adder_7 (.a(a6), .b(b6), .out(s6), .cin(adder_6_cout), .cout(adder_7_cout));
  Adder #(.width(1)) adder_8 (.a(a7), .b(b7), .out(s7), .cin(adder_7_cout), .cout(c));
endmodule

module addShiftMultiplier (
  input  clk,
  input  rst,
  input  en,
  input  b0,
  input  b1,
  input  b2,
  input  b3,
  input  b4,
  input  b5,
  input  b6,
  input  b7,
  input  a0,
  input  debouncerBC,
  input  a1,
  input  a2,
  input  a3,
  input  a4,
  input  a5,
  input  a6,
  input  a7,
  output p15,
  output out_22,
  output out_23,
  output out_24,
  output out_25,
  output out_26,
  output out_27,
  output out_28,
  output out_29,
  output out_30,
  output out_31,
  output out_32,
  output out_33,
  output out_34,
  output out_35,
  output p0
);

  wire multiplexer_1_out, multiplexer_2_out, multiplexer_3_out, multiplexer_4_out, multiplexer_5_out,
       multiplexer_6_out, multiplexer_7_out, multiplexer_8_out, multiplexer_9_out, multiplexer_10_out,
       multiplexer_11_out, multiplexer_12_out, rca8bits_1_c, rca8bits_1_s0, rca8bits_1_s1, rca8bits_1_s2,
       rca8bits_1_s3, rca8bits_1_s4, rca8bits_1_s5, rca8bits_1_s6, rca8bits_1_s7, shift_register_1_p13,
       shift_register_1_p14, shift_register_1_p15, shift_register_1_p16, shift_register_1_p17,
       shift_register_1_p18, shift_register_1_p19, shift_register_1_p20, shift_register_2_p14,
       shift_register_2_p15, shift_register_2_p16, shift_register_2_p17;

  // Shift_Register shift_register_1: pin names not known; wires that end beside it: rst, en, 1'b0, clk, a0, a1, a2, a3, a4, a5, a6, a7, shift_register_1_p13, shift_register_1_p14, shift_register_1_p15, shift_register_1_p16, shift_register_1_p17, shift_register_1_p18, shift_register_1_p19, shift_register_1_p20
  Multiplexer multiplexer_1 (.in0(1'b0), .in1(shift_register_1_p13), .out(multiplexer_1_out), .sel(p0));
  Multiplexer multiplexer_2 (.in0(1'b0), .in1(shift_register_1_p14), .out(multiplexer_2_out), .sel(p0));
  Multiplexer multiplexer_3 (.in0(1'b0), .in1(shift_register_1_p15), .out(multiplexer_3_out), .sel(p0));
  Multiplexer multiplexer_4 (.in0(1'b0), .in1(shift_register_1_p16), .out(multiplexer_4_out), .sel(p0));
  Multiplexer multiplexer_5 (.in0(1'b0), .in1(shift_register_1_p17), .out(multiplexer_5_out), .sel(p0));
  Multiplexer multiplexer_6 (.in0(1'b0), .in1(shift_register_1_p18), .out(multiplexer_6_out), .sel(p0));
  Multiplexer multiplexer_7 (.in0(1'b0), .in1(shift_register_1_p19), .out(multiplexer_7_out), .sel(p0));
  Multiplexer multiplexer_8 (.in0(1'b0), .in1(shift_register_1_p20), .out(multiplexer_8_out), .sel(p0));
  RCA8Bits rca8bits_1 (
    .cin(rca8bits_1_c), .a0(multiplexer_1_out), .b0(out_27), .a1(multiplexer_2_out), .b1(out_26),
    .a2(multiplexer_3_out), .b2(out_25), .a3(multiplexer_4_out), .b3(out_24), .a4(multiplexer_5_out),
    .b4(out_23), .a5(multiplexer_6_out), .b5(out_22), .a6(multiplexer_7_out), .b6(p15),
    .a7(multiplexer_8_out), .b7(1'b0), .s0(rca8bits_1_s0), .s1(rca8bits_1_s1), .s2(rca8bits_1_s2),
    .s3(rca8bits_1_s3), .s4(rca8bits_1_s4), .s5(rca8bits_1_s5), .s6(rca8bits_1_s6), .s7(rca8bits_1_s7),
    .c(rca8bits_1_c));
  // Shift_Register #(.length(16)) shift_register_2: pin names not known; wires that end beside it: rst, en, en, clk, 1'b0, rca8bits_1_s7, rca8bits_1_s6, rca8bits_1_s5, rca8bits_1_s4, rca8bits_1_s3, rca8bits_1_s2, rca8bits_1_s1, rca8bits_1_s0, shift_register_2_p14, shift_register_2_p15, shift_register_2_p16, shift_register_2_p17, p15, out_22, out_23, out_24, out_25, out_26, out_27, out_28, out_29, out_30, out_31, out_32
  Multiplexer multiplexer_9 (.in0(out_35), .in1(b0), .out(multiplexer_9_out), .sel(debouncerBC));
  Multiplexer multiplexer_10 (.in0(out_34), .in1(b1), .out(multiplexer_10_out), .sel(debouncerBC));
  Multiplexer multiplexer_11 (.in0(out_33), .in1(b2), .out(multiplexer_11_out), .sel(debouncerBC));
  Multiplexer multiplexer_12 (.in0(out_32), .in1(b3), .out(multiplexer_12_out), .sel(debouncerBC));
  Multiplexer multiplexer_13 (.in0(out_31), .in1(b4), .out(shift_register_2_p17), .sel(debouncerBC));
  Multiplexer multiplexer_14 (.in0(out_30), .in1(b5), .out(shift_register_2_p16), .sel(debouncerBC));
  Multiplexer multiplexer_15 (.in0(out_29), .in1(b6), .out(shift_register_2_p15), .sel(debouncerBC));
  Multiplexer multiplexer_16 (.in0(out_28), .in1(b7), .out(shift_register_2_p14), .sel(debouncerBC));
endmodule

module twosComp8 (
  input  a0,
  input  a1,
  input  a2,
  input  a3,
  input  a4,
  input  a5,
  input  a6,
  input  a7,
  output z0,
  output z1,
  output z2,
  output z3,
  output z4,
  output z5,
  output z6,
  output z7
);

  wire and_1_out, and_2_out, and_3_out, and_4_out, and_5_out, and_6_out, and_7_out, not_1_out, not_2_out,
       not_3_out, not_4_out, not_5_out, not_6_out, not_7_out, not_8_out;

  not not_1 (not_1_out, a0);
  not not_2 (not_2_out, a1);
  not not_3 (not_3_out, a2);
  not not_4 (not_4_out, a3);
  not not_5 (not_5_out, a4);
  not not_6 (not_6_out, a5);
  not not_7 (not_7_out, a6);
  not not_8 (not_8_out, a7);
  and and_1 (and_1_out, not_1_out, not_1_out);
  and and_2 (and_2_out, and_1_out, not_2_out);
  and and_3 (and_3_out, and_2_out, not_3_out);
  and and_4 (and_4_out, and_3_out, not_4_out);
  and and_5 (and_5_out, and_4_out, not_5_out);
  and and_6 (and_6_out, and_5_out, not_6_out);
  and and_7 (and_7_out, and_6_out, not_7_out);
  not not_9 (z0, not_1_out);
  xor xor_1 (z1, and_1_out, not_2_out);
  xor xor_2 (z2, and_2_out, not_3_out);
  xor xor_3 (z3, and_3_out, not_4_out);
  xor xor_4 (z4, and_4_out, not_5_out);
  xor xor_5 (z5, and_5_out, not_6_out);
  xor xor_6 (z6, and_6_out, not_7_out);
  xor xor_7 (z7, and_7_out, not_8_out);
endmodule

module twosComp16 (
  input  LSB,
  input  in_2,
  input  in_3,
  input  in_4,
  input  in_5,
  input  in_6,
  input  in_7,
  input  in_8,
  input  in_9,
  input  in_10,
  input  in_11,
  input  in_12,
  input  in_13,
  input  in_14,
  input  in_15,
  input  in_16,
  output LSBz,
  output out_18,
  output out_19,
  output out_20,
  output out_21,
  output out_22,
  output out_23,
  output out_24,
  output out_25,
  output out_26,
  output out_27,
  output out_28,
  output out_29,
  output out_30,
  output out_31,
  output out_32
);

  wire and_1_out, and_2_out, and_3_out, and_4_out, and_5_out, and_6_out, and_7_out, and_8_out, and_9_out,
       and_10_out, and_11_out, and_12_out, and_13_out, and_14_out, and_15_out, not_1_out, not_2_out,
       not_3_out, not_4_out, not_5_out, not_6_out, not_7_out, not_8_out, not_9_out, not_10_out, not_11_out,
       not_12_out, not_13_out, not_14_out, not_15_out, not_16_out;

  not not_1 (not_1_out, LSB);
  not not_2 (not_2_out, in_2);
  not not_3 (not_3_out, in_3);
  not not_4 (not_4_out, in_4);
  not not_5 (not_5_out, in_5);
  not not_6 (not_6_out, in_6);
  not not_7 (not_7_out, in_7);
  not not_8 (not_8_out, in_8);
  not not_9 (not_9_out, in_9);
  not not_10 (not_10_out, in_10);
  not not_11 (not_11_out, in_11);
  not not_12 (not_12_out, in_12);
  not not_13 (not_13_out, in_13);
  not not_14 (not_14_out, in_14);
  not not_15 (not_15_out, in_15);
  not not_16 (not_16_out, in_16);
  and and_1 (and_1_out, not_1_out, not_1_out);
  and and_2 (and_2_out, and_1_out, not_2_out);
  and and_3 (and_3_out, and_2_out, not_3_out);
  and and_4 (and_4_out, and_3_out, not_4_out);
  and and_5 (and_5_out, and_4_out, not_5_out);
  and and_6 (and_6_out, and_5_out, not_6_out);
  and and_7 (and_7_out, and_6_out, not_7_out);
  and and_8 (and_8_out, and_7_out, not_8_out);
  and and_9 (and_9_out, and_8_out, not_9_out);
  and and_10 (and_10_out, and_9_out, not_10_out);
  and and_11 (and_11_out, and_10_out, not_11_out);
  and and_12 (and_12_out, and_11_out, not_12_out);
  and and_13 (and_13_out, and_12_out, not_13_out);
  and and_14 (and_14_out, and_13_out, not_14_out);
  and and_15 (and_15_out, and_14_out, not_15_out);
  not not_17 (LSBz, not_1_out);
  xor xor_1 (out_18, and_1_out, not_2_out);
  xor xor_2 (out_19, and_2_out, not_3_out);
  xor xor_3 (out_20, and_3_out, not_4_out);
  xor xor_4 (out_21, and_4_out, not_5_out);
  xor xor_5 (out_22, and_5_out, not_6_out);
  xor xor_6 (out_23, and_6_out, not_7_out);
  xor xor_7 (out_24, and_7_out, not_8_out);
  xor xor_8 (out_25, and_8_out, not_9_out);
  xor xor_9 (out_26, and_9_out, not_10_out);
  xor xor_10 (out_27, and_10_out, not_11_out);
  xor xor_11 (out_28, and_11_out, not_12_out);
  xor xor_12 (out_29, and_12_out, not_13_out);
  xor xor_13 (out_30, and_13_out, not_14_out);
  xor xor_14 (out_31, and_14_out, not_15_out);
  xor xor_15 (out_32, and_15_out, not_16_out);
endmodule

module threeSvnSeg (
  input  L,
  input  R,
  output Z2,
  output Z1
);

  wire and_1_out, and_2_out, and_3_out, and_4_out, and_5_out, and_6_out, and_7_out, clock_1_out, d_ff_1_qn,
       d_ff_2_qn, not_1_out, not_2_out, or_1_out, or_2_out;

  Clock clock_1 (.out(clock_1_out));
  not not_1 (not_1_out, L);
  not not_2 (not_2_out, R);
  and and_1 (and_1_out, Z1, not_2_out, not_1_out);
  and and_2 (and_2_out, Z1, R, L);
  and and_3 (and_3_out, Z2, not_2_out, L);
  and and_4 (and_4_out, not_1_out, R, d_ff_1_qn, d_ff_2_qn);
  and and_5 (and_5_out, Z2, not_1_out);
  and and_6 (and_6_out, Z2, R);
  and and_7 (and_7_out, not_1_out, R, Z1);
  or or_1 (or_1_out, and_1_out, and_2_out, and_3_out, and_4_out);
  or or_2 (or_2_out, and_5_out, and_6_out, and_7_out);
  D_Flip_Flop d_ff_1 (.D(or_2_out), .clk(clock_1_out), .Q(Z2), .Qn(d_ff_1_qn));  // open: preset, reset
  D_Flip_Flop d_ff_2 (.D(or_1_out), .clk(clock_1_out), .Q(Z1), .Qn(d_ff_2_qn));  // open: preset, reset
endmodule
